# Fritzing sketch mpu6050 (saved by Fritzing 0.9.3b)

parts:
  Part1 = Arduino Uno (Rev3)
  GY1 = MPU-6050 [form="♀ (female)" package=THT]

nets:
  N1: Part1.A4/SDA, GY1.pin4
  N2: Part1.A5/SCL, GY1.pin3
  N3: Part1.D2, GY1.pin8
  N4: Part1.5V, GY1.pin1
  N5: Part1.GND, GY1.pin2

custom parts:
  MPU-6050: Accellerometro e Giroscopio MPU-6050
